# Fritzing sketch Circuit_Diagram (saved by Fritzing 0.9.3b)
circuit board: 8.46667cm x 5.64444cm
stripboards: 1

parts:
  U1 = ESP8266 WiFi Module [part_number=ESP8266]
  J1 = male pin header, 1 pin [form="♂ (male)"]
  J2 = male pin header, 1 pin [form="♂ (male)"]
  J3 = male pin header, 1 pin [form="♂ (male)"]
  J4 = male pin header, 1 pin [form="♂ (male)"]
  J5 = male pin header, 1 pin [form="♂ (male)"]
  J6 = male pin header, 1 pin [form="♂ (male)"]
  J8 = male pin header, 1 pin [form="♂ (male)"]
  J7 = male pin header, 1 pin [form="♂ (male)"]
  J9 = male pin header, 1 pin [form="♂ (male)"]
  J10 = male pin header, 1 pin [form="♂ (male)"]
  J11 = male pin header, 1 pin [form="♂ (male)"]
  J12 = male pin header, 1 pin [form="♂ (male)"]

nets:
  N1: U1.VCC, J8.pin1, J12.pin1
  N2: U1.GPIO_0, J10.pin1
  N3: U1.GND, J5.pin1, J9.pin1, J11.pin1
  N4: J1.pin1, J3.pin1
  N5: J2.pin1, J4.pin1
  N6: J6.pin1, J7.pin1

notes:
  +
  -

custom parts:
  ESP8266 WiFi Module: Generic WiFi Module based on the ESP8266 with onboard PCB antenna and UART communications
